# Fritzing sketch power (saved by Fritzing 0.9.6b)
circuit board: 8.47cm x 5.64444cm
breadboards: 1

parts:
  D1 = SOLAR-IXYS [package=solarbit-12x1]
  D2 = SOLAR-IXYS [package=solarbit-12x1]
  D3 = SOLAR-IXYS [package=solarbit-12x1]
  BAT1 = Battery Holders [package=lipo-1100mAh]
  TP1 = TP4056 [chip_label=TP4056 package="DIP (Dual Inline) [THT]"]
  U2 = Voltage Regulator - 3.3V [part_number=MCP1700 package="TO220 [THT]"]
  U3 = SWITCH_SPDT [package=kps-1290]
  JP1 = Header 2 [package=jst-2-pth-ns]
  C1 = Capacitor Polarized [package=cpol-radial-100uf-25v]
  C2 = Ceramic Capacitor [capacitance="100 nF" voltage=35V package="1206 [SMD, multilayer]"]

nets (from the breadboard view):
  N1: D1.A, D2.A, D3.A, TP1.pin2
  N2: D1.C, D2.C, D3.C, TP1.pin1
  N3: BAT1.+, TP1.pin3, U2.input_voltage
  N4: BAT1.-, TP1.pin6, U2.GND, JP1.1, C1.-, C2.0
  N5: U2.output_voltage, U3.P
  N6: U3.S, JP1.2, C1.+, C2.1

custom parts:
  TP4056: A DIP stand-in part for whatever IC you want. With 6 pins on a 300mil dual inline package (DIP) footprint.
